# Fritzing sketch Nice (saved by Fritzing 0.8.3b)

parts:
  Part1 = Arduino Nano (Rev3.0)
  Part2 = 3-Axis Accelerometer Breakout - MMA8452Q
  U1 = Bluetooth Chipset CSR [part_number=bc417143]

nets:
  N1: Part1.D2, U1.RX
  N2: Part1.D3, U1.TX
  GND: Part1.GND, Part2.GND
  N3: Part1.A5, Part2.SCL
  N4: Part1.A4, Part2.SDA
  3V3: Part1.3V3, U1.VCC

custom parts:
  Bluetooth Chipset CSR: Bluetooth module uses CSR Bluecore4
